# Fritzing sketch Otis Lite Prefboard (saved by Fritzing 1.0.5)
perfboards: 1

parts:
  Pico/Pico2_Mod_1 = Raspberry Pi Pico or Pico 2
  R1 = Resistor [tolerance=±5% power=0.25W resistance=150 package=THT]  # not connected
  R2 = Resistor [tolerance=±5% power=0.25W resistance=150 package=THT]  # not connected
  R3 = Resistor [tolerance=±5% power=0.25W resistance=150 package=THT]  # not connected
  R4 = Resistor [tolerance=±5% power=0.25W resistance=150 package=THT]  # not connected
  R5 = Resistor [tolerance=±5% power=0.25W resistance=10k package=THT]
  LED1 = LED - 5mm [color="Red (633nm)" current=0.030A package="5 mm [THT]"]  # not connected
  LED2 = LED - 5mm [color="Red (633nm)" current=0.030A package="5 mm [THT]"]  # not connected
  LED3 = LED - 5mm [color="Red (633nm)" current=0.030A package="5 mm [THT]"]  # not connected
  LED4 = LED - 5mm [color="Red (633nm)" current=0.030A package="5 mm [THT]"]  # not connected
  R6 = Resistor [tolerance=±5% power=0.25W resistance=10k package=THT]  # not connected
  R7 = Resistor [tolerance=±5% power=0.25W resistance=10k package=THT]
  S1 = Round Pushbutton  # not connected
  S2 = Round Pushbutton  # not connected
  S3 = Round Pushbutton  # not connected
  JP2 = USB_MICROB_PLUG [package=micro-b-ra-th]
  JP3 = USB_MICROB_PLUG [package=micro-b-ra-th]
  R8 = Resistor [tolerance=±5% power=0.25W resistance=5.1k package=THT]

nets:
  N1: Pico/Pico2_Mod_1.pin_3, Pico/Pico2_Mod_1.pin_8, Pico/Pico2_Mod_1.pin_13, Pico/Pico2_Mod_1.pin_18, Pico/Pico2_Mod_1.pin_23, Pico/Pico2_Mod_1.pin_28, Pico/Pico2_Mod_1.pin_33, Pico/Pico2_Mod_1.pin_38
  N2: Pico/Pico2_Mod_1.pin_40, JP3.VCC
  N3: R5.Pin_1, R7.Pin_1
  N4: JP2.D-, JP3.D-
  N5: JP2.D+, JP3.D+
  N6: JP3.ID, R8.Pin_1

notes:
  Green cable used for CC. The CC pin must be connected to GND through a 5.1 kΩ resistor. Usually, there are two CC pins (CC1 and CC2), but in my connector they are soldered together.

custom parts:
  Raspberry Pi Pico or Pico 2: Raspberry Pi Pico and Pico 2. Based around the RP2040 and RP2350 microcontrollers respectively, Picos are low cost microcontroller device bringing Raspberry Pi quality, cost, and easy of use to the microcontroller space. Jan 2021, Split part in to two versions: tht (this one) and SMD. This one will drill holes for a .1 in header in pcb to allow plugging in the module as well as providing pads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
